// Logisim project regfile.circ as structural Verilog: 1 circuit, main circuit regfile
module regfile (
  input  [4:0] ReadIndex1,
  input  [4:0] ReadIndex2,
  input  [4:0] WriteIndex,
  input  [31:0] WriteData,
  input  RegWEn,
  input  clk,
  output [31:0] ra,
  output [31:0] sp,
  output [31:0] t0,
  output [31:0] t1,
  output [31:0] t2,
  output [31:0] s0,
  output [31:0] s1,
  output [31:0] a0,
  output [31:0] ReadData1,
  output [31:0] ReadData2
);

  wire a0_en, a1_en, a2_en, a3_en, a4_en, a5_en, a6_en, a7_en, gp_en, ra_en, s0_en, s1_en, s2_en, s3_en,
       s4_en, s5_en, s6_en, s7_en, s8_en, s9_en, s10_en, s11_en, sp_en, t0_en, t1_en, t2_en, t3_en, t4_en,
       t5_en, t6_en, tp_en;
  wire [31:0] a1, a2, a3, a4, a5, a6, a7, gp, s2, s3, s4, s5, s6, s7, s8, s9, s10, s11, t3, t4, t5, t6, tp,
       zero;

  Register #(.width(32)) s8_reg (.D(WriteData), .en(s8_en), .clk(clk), .Q(s8));  // open: clr
  Register #(.width(32)) s9_reg (.D(WriteData), .en(s9_en), .clk(clk), .Q(s9));  // open: clr
  Register #(.width(32)) s10_reg (.D(WriteData), .en(s10_en), .clk(clk), .Q(s10));  // open: clr
  Register #(.width(32)) s11_reg (.D(WriteData), .en(s11_en), .clk(clk), .Q(s11));  // open: clr
  Register #(.width(32)) zero_reg (.Q(zero));  // open: D, en, clk, clr
  Register #(.width(32)) ra_reg (.D(WriteData), .en(ra_en), .clk(clk), .Q(ra));  // open: clr
  Register #(.width(32)) sp_reg (.D(WriteData), .en(sp_en), .clk(clk), .Q(sp));  // open: clr
  Register #(.width(32)) gp_reg (.D(WriteData), .en(gp_en), .clk(clk), .Q(gp));  // open: clr
  Register #(.width(32)) tp_reg (.D(WriteData), .en(tp_en), .clk(clk), .Q(tp));  // open: clr
  Register #(.width(32)) t0_reg (.D(WriteData), .en(t0_en), .clk(clk), .Q(t0));  // open: clr
  Register #(.width(32)) t1_reg (.D(WriteData), .en(t1_en), .clk(clk), .Q(t1));  // open: clr
  Register #(.width(32)) t2_reg (.D(WriteData), .en(t2_en), .clk(clk), .Q(t2));  // open: clr
  Register #(.width(32)) s0_reg (.D(WriteData), .en(s0_en), .clk(clk), .Q(s0));  // open: clr
  Register #(.width(32)) s1_reg (.D(WriteData), .en(s1_en), .clk(clk), .Q(s1));  // open: clr
  Register #(.width(32)) a0_reg (.D(WriteData), .en(a0_en), .clk(clk), .Q(a0));  // open: clr
  Register #(.width(32)) a1_reg (.D(WriteData), .en(a1_en), .clk(clk), .Q(a1));  // open: clr
  Register #(.width(32)) a2_reg (.D(WriteData), .en(a2_en), .clk(clk), .Q(a2));  // open: clr
  Register #(.width(32)) a3_reg (.D(WriteData), .en(a3_en), .clk(clk), .Q(a3));  // open: clr
  Register #(.width(32)) a4_reg (.D(WriteData), .en(a4_en), .clk(clk), .Q(a4));  // open: clr
  Register #(.width(32)) a5_reg (.D(WriteData), .en(a5_en), .clk(clk), .Q(a5));  // open: clr
  Demultiplexer #(.select(5)) demultiplexer_1 (
    .out1(ra_en), .out2(sp_en), .out3(gp_en), .out4(tp_en), .out5(t0_en), .out6(t1_en), .out7(t2_en),
    .out8(s0_en), .out9(s1_en), .out10(a0_en), .out11(a1_en), .out12(a2_en), .out13(a3_en), .out14(a4_en),
    .out15(a5_en), .out16(a6_en), .out17(a7_en), .out18(s2_en), .out19(s3_en), .out20(s4_en), .out21(s5_en),
    .out22(s6_en), .out23(s7_en), .out24(s8_en), .out25(s9_en), .out26(s10_en), .out27(s11_en),
    .out28(t3_en), .out29(t4_en), .out30(t5_en), .out31(t6_en), .in(RegWEn), .sel(WriteIndex));  // open: out0
  Register #(.width(32)) a6_reg (.D(WriteData), .en(a6_en), .clk(clk), .Q(a6));  // open: clr
  Register #(.width(32)) a7_reg (.D(WriteData), .en(a7_en), .clk(clk), .Q(a7));  // open: clr
  Register #(.width(32)) s2_reg (.D(WriteData), .en(s2_en), .clk(clk), .Q(s2));  // open: clr
  Register #(.width(32)) s3_reg (.D(WriteData), .en(s3_en), .clk(clk), .Q(s3));  // open: clr
  Multiplexer #(.select(5), .width(32)) multiplexer_1 (
    .in0(zero), .in1(ra), .in2(sp), .in3(gp), .in4(tp), .in5(t0), .in6(t1), .in7(t2), .in8(s0), .in9(s1),
    .in10(a0), .in11(a1), .in12(a2), .in13(a3), .in14(a4), .in15(a5), .in16(a6), .in17(a7), .in18(s2),
    .in19(s3), .in20(s4), .in21(s5), .in22(s6), .in23(s7), .in24(s8), .in25(s9), .in26(s10), .in27(s11),
    .in28(t3), .in29(t4), .in30(t5), .in31(t6), .out(ReadData1), .sel(ReadIndex1));
  Register #(.width(32)) s4_reg (.D(WriteData), .en(s4_en), .clk(clk), .Q(s4));  // open: clr
  Register #(.width(32)) s5_reg (.D(WriteData), .en(s5_en), .clk(clk), .Q(s5));  // open: clr
  Register #(.width(32)) s6_reg (.D(WriteData), .en(s6_en), .clk(clk), .Q(s6));  // open: clr
  Register #(.width(32)) s7_reg (.D(WriteData), .en(s7_en), .clk(clk), .Q(s7));  // open: clr
  Register #(.width(32)) t3_reg (.D(WriteData), .en(t3_en), .clk(clk), .Q(t3));  // open: clr
  Register #(.width(32)) t4_reg (.D(WriteData), .en(t4_en), .clk(clk), .Q(t4));  // open: clr
  Register #(.width(32)) t5_reg (.D(WriteData), .en(t5_en), .clk(clk), .Q(t5));  // open: clr
  Register #(.width(32)) t6_reg (.D(WriteData), .en(t6_en), .clk(clk), .Q(t6));  // open: clr
  Multiplexer #(.select(5), .width(32)) multiplexer_2 (
    .in0(zero), .in1(ra), .in2(sp), .in3(gp), .in4(tp), .in5(t0), .in6(t1), .in7(t2), .in8(s0), .in9(s1),
    .in10(a0), .in11(a1), .in12(a2), .in13(a3), .in14(a4), .in15(a5), .in16(a6), .in17(a7), .in18(s2),
    .in19(s3), .in20(s4), .in21(s5), .in22(s6), .in23(s7), .in24(s8), .in25(s9), .in26(s10), .in27(s11),
    .in28(t3), .in29(t4), .in30(t5), .in31(t6), .out(ReadData2), .sel(ReadIndex2));

  // Notes on the sheet:
  //   INPUTS to your circuit
  //   DON'T CHANGE THE LOCATIONS OF THE INPUTS AND OUTPUTS!
  //   These are DEBUG/TEST outputs from your circuit.
  //   OUTPUTS from your circuit
endmodule
